# Fritzing sketch Full Radio (saved by Fritzing 0.9.4)
breadboards: 1

parts:
  bDown = Pushbutton [package=THT]
  Mute = Pushbutton [package=THT]
  sUp = Pushbutton [package=THT]
  sDown = Pushbutton [package=THT]
  bUp = Pushbutton [package=THT]
  LCD1 = LCD screen
  R1 = Resistor [tolerance=±5% resistance=1k package="0402 [SMD]"]
  R2 = Resistor [tolerance=±5% resistance=1k package="0402 [SMD]"]
  R3 = Resistor [tolerance=±5% resistance=1k package="0402 [SMD]"]
  R4 = Resistor [tolerance=±5% resistance=1k package="0402 [SMD]"]
  R5 = Resistor [tolerance=±5% resistance=1k package="0402 [SMD]"]
  Part1 = Arduino Pro Mini (5V)
  R6 = Trimmer Potentiometer [maximum_resistance=10kΩ package=THT]
  IC1 = IC, DIP package, 10 pins [chip_label=TEA5767]
  U3 = LM 358 Dual Op-Amp [package="DIP8 [THT]"]
  U4 = LM 358 Dual Op-Amp [package="DIP8 [THT]"]
  ANT1 = Antenna
  R7 = Trimmer Potentiometer [maximum_resistance=10kΩ package=THT]
  R8 = Trimmer Potentiometer [maximum_resistance=10kΩ package=THT]
  BAT1 = BC9VPC [package=bc9vpc]
  C3 = Electrolytic Capacitor [capacitance=22µF package="100 mil [THT, electrolytic]"]
  C4 = Electrolytic Capacitor [capacitance=10µF package="100 mil [THT, electrolytic]"]
  R9 = Resistor [tolerance=±5% resistance=10 package="0402 [SMD]"]
  C5 = Electrolytic Capacitor [capacitance=10µF package="100 mil [THT, electrolytic]"]
  R10 = Resistor [tolerance=±5% resistance=10 package="0402 [SMD]"]
  C2 = Electrolytic Capacitor [capacitance=22µF package="100 mil [THT, electrolytic]"]
  C6 = Capacitor Polarized [package=cpol-radial-100uf-25v]
  C7 = Capacitor Polarized [package=cpol-radial-100uf-25v]
  Right_Speaker = Camdenboss CTB0158-2 [part_number=CTB0158-2 package=THT]
  Left_Speaker = Camdenboss CTB0158-2 [part_number=CTB0158-2 package=THT]
  IC2 = Voltage Regulator [package=to-220-alt]
  C8 = Electrolytic Capacitor [capacitance=10µF package="100 mil [THT, electrolytic]"]
  C9 = Electrolytic Capacitor [capacitance=10µF package="100 mil [THT, electrolytic]"]

nets:
  VSS: bDown.leg0, Mute.leg0, sUp.leg0, sDown.leg0, bUp.leg0, LCD1.VSS, LCD1.R/W, LCD1.LED-, Part1.GND, R6.leg1, IC1.pin3, IC1.pin6, U3.connector1, U3.connector3, U4.connector1, U4.connector3, R7.leg2, R8.leg2, BAT1.V-, C3.-, R9.Pin_1, R10.Pin_0, C2.-, Right_Speaker.pin1, Left_Speaker.pin2
  N1: bDown.leg1, R4.Pin_0, Part1.D6
  N2: Mute.leg1, R5.Pin_0, Part1.D8
  N3: sUp.leg1, R1.Pin_0, Part1.A2
  N4: sDown.leg1, R2.Pin_0, Part1.SCK
  N5: bUp.leg1, R3.Pin_0, Part1.D7
  VDD: LCD1.VDD, LCD1.LED+, R1.Pin_1, R2.Pin_1, R3.Pin_1, R4.Pin_1, R5.Pin_1, Part1.VCC, R6.leg2, IC1.pin5, IC2.OUT, C8.+
  N6: LCD1.V0, R6.wiper
  N7: LCD1.RS, Part1.D10
  N8: LCD1.E, Part1.D9
  N9: LCD1.DB4, Part1.D5
  N10: LCD1.DB5, Part1.D4
  N11: LCD1.DB6, Part1.D3
  N12: LCD1.DB7, Part1.D2
  N13: Part1.A4, IC1.pin1
  N14: Part1.A5, IC1.pin2
  N15: IC1.pin7, R7.leg1
  N16: IC1.pin8, R8.leg1
  N17: IC1.pin10, ANT1.antenna_lead
  N18: U3.connector2, R7.wiper
  N19: U3.connector4, C4.+, C7.+
  N20: U3.connector5, U4.connector5, BAT1.V+, IC2.GND, C9.+
  N21: U3.connector6, C3.+
  N22: U4.connector2, R8.wiper
  N23: U4.connector4, C5.+, C6.+
  N24: U4.connector6, C2.+
  N25: C4.-, R9.Pin_0
  N26: C5.-, R10.Pin_1
  N27: C6.-, Right_Speaker.pin2
  N28: C7.-, Left_Speaker.pin1
  N29: IC2.IN, C8.-, C9.-
